# Fritzing sketch Interfatare CJMU GUVA-S12SD cu Arduino UNO (saved by Fritzing 0.9.3b)

parts:
  Part1 = GUVA-S12SD UV Light Sensor
  Part2 = Arduino Uno (Rev3)

nets:
  5V: Part1.5V, Part2.5V
  N1: Part1.Out, Part2.GND
  N2: Part1.GND, Part2.A0

custom parts:
  GUVA-S12SD UV Light Sensor: Extend your light-sensing spectrum with this analog UV sensor module. It uses a UV photodiode, which can detect the 240-370nm range of light (which covers UVB and most of UVA spectrum). The signal level from the photodiode is very small, in the nano-ampere level, so we tossed on an opamp to amplify the signal to a more manageable volt-level.
